// Logisim project JMP.circ as structural Verilog: 1 circuit, main circuit main
module main (
  input  [3:0] NEM,
  input  [3:0] RF2,
  input  [3:0] RF1,
  input  [3:0] RD,
  input  Bbit,
  input  [15:0] in_6,
  input  [15:0] PC,
  output [15:0] INM,
  output [15:0] PCdata,
  output Jact
);

  wire demultiplexer_1_p4, demultiplexer_1_p6, demultiplexer_1_p7;
  wire [15:0] and_1_out, demultiplexer_1_p5;
  wire [15:1] undriven, undriven_2;

  assign and_1_out = demultiplexer_1_p5 & {undriven, Bbit};  // AND_Gate and_1, 16 bits wide
  assign PCdata = demultiplexer_1_p7 ? PC : 16'bz;  // Controlled_Buffer controlled_buffer_1
  // Demultiplexer #(.select(4), .width(16)) demultiplexer_1: pin names not known; wires that end beside it: NEM, INM, 1'b1, demultiplexer_1_p4, demultiplexer_1_p5, demultiplexer_1_p6, demultiplexer_1_p7
  assign INM = demultiplexer_1_p4 ? {4'b1111, RD, RF1, RF2} : 16'bz;  // Controlled_Buffer controlled_buffer_2
  assign INM = demultiplexer_1_p4 ? {undriven_2, 1'b1} : 16'bz;  // Controlled_Buffer controlled_buffer_3
  Controlled_Buffer #(.width(16)) controlled_buffer_4 (.out(INM), .en(demultiplexer_1_p6));  // open: in
  assign INM = and_1_out[0] ? {4'b1111, RD, RF1, RF2} : 16'bz;  // Controlled_Buffer controlled_buffer_5
  Controlled_Buffer #(.width(16)) controlled_buffer_6 (.in({undriven_2, 1'b1}), .en(and_1_out[0]));  // open: out
  // Pins of 1 and 16 bits meet at {undriven, Bbit}
  // Pins of 1 and 16 bits meet at {undriven_2, 1'b1}
  // Pins of 1 and 16 bits meet at INM
  // Pins of 1 and 16 bits meet at and_1_out

  assign Jact = INM[0];
endmodule
